// Digital circuit ALU.dig as structural Verilog
module ALU (
  input  En,
  input  [3:0] Opcode,
  input  [15:0] A,
  input  [15:0] B,
  input  CLK,
  input  Carry_In,
  input  Borrow_In,
  output [15:0] Sum,
  output Carry_Out,
  output Borrow_Out,
  output [15:0] Sub,
  output [15:0] mul_low,
  output [15:0] mul_high,
  output [15:0] AND,
  output [15:0] XOR,
  output [15:0] OR,
  output [15:0] Not,
  output [15:0] SAR,
  output [15:0] SHR,
  output [15:0] SHL
);

  wire _16_bitmuxwithenablepin_1_q0, _16_bitmuxwithenablepin_1_q1, _16_bitmuxwithenablepin_1_q2,
       _16_bitmuxwithenablepin_1_q3, _16_bitmuxwithenablepin_1_q4, _16_bitmuxwithenablepin_1_q5,
       _16_bitmuxwithenablepin_1_q6, _16_bitmuxwithenablepin_1_q7, _16_bitmuxwithenablepin_1_q8,
       _16_bitmuxwithenablepin_1_q9, _16_bitmuxwithenablepin_1_q10, _16_bitmuxwithenablepin_1_q11,
       _16_bitmuxwithenablepin_1_q12, _16_bitmuxwithenablepin_1_q13, _16_bitmuxwithenablepin_1_q14,
       _16_bitmuxwithenablepin_1_q15, alu_regctrl_1_q_0, alu_regctrl_1_q_1, alu_regctrl_1_q_2,
       alu_regctrl_1_q_3, alu_regctrl_1_q_4, alu_regctrl_1_q_5, alu_regctrl_1_q_6, alu_regctrl_1_q_7,
       alu_regctrl_1_q_8, alu_regctrl_1_q_9, alu_regctrl_1_q_a, alu_regctrl_1_rst, not_1_out, not_2_out,
       not_5_out, not_6_out, not_9_out, not_11_out, not_13_out, not_15_out, not_17_out, not_19_out,
       not_21_out, not_23_out, not_25_out, not_27_out, not_29_out, not_31_out, not_33_out, not_34_out,
       not_35_out, not_37_out, not_38_out, not_39_out, not_41_out, not_42_out;
  wire [4:0] _5_bit_reg_2_q, _5_bit_reg_3_q, _5_bit_reg_q, alu_regrst_2_q;
  wire [15:0] alu_regrst_1_q, mul_2_mul, undriven, undriven_2, undriven_3, undriven_4, undriven_5,
       undriven_6, undriven_7, undriven_8, undriven_9, undriven_10, undriven_11, undriven_12, undriven_13,
       undriven_14, undriven_15, undriven_16, undriven_17, undriven_18;
  wire [15:5] alu_regrst_2_q_2;
  wire [31:16] mul_1_mul;

  _16_BitMuxWithEnablePin _16_bitmuxwithenablepin_1 (
    .EN(En), .Sel_4Bit(Opcode), .Q0(_16_bitmuxwithenablepin_1_q0), .Q1(_16_bitmuxwithenablepin_1_q1),
    .Q2(_16_bitmuxwithenablepin_1_q2), .Q3(_16_bitmuxwithenablepin_1_q3), .Q4(_16_bitmuxwithenablepin_1_q4),
    .Q5(_16_bitmuxwithenablepin_1_q5), .Q6(_16_bitmuxwithenablepin_1_q6), .Q7(_16_bitmuxwithenablepin_1_q7),
    .Q8(_16_bitmuxwithenablepin_1_q8), .Q9(_16_bitmuxwithenablepin_1_q9),
    .Q10(_16_bitmuxwithenablepin_1_q10), .Q11(_16_bitmuxwithenablepin_1_q11),
    .Q12(_16_bitmuxwithenablepin_1_q12), .Q13(_16_bitmuxwithenablepin_1_q13),
    .Q14(_16_bitmuxwithenablepin_1_q14), .Q15(_16_bitmuxwithenablepin_1_q15));
  ALU_RegCtrl alu_regctrl_1 (
    .IsEn__MUX(En), .CLK(CLK), ._0x0(_16_bitmuxwithenablepin_1_q0), ._0x1(_16_bitmuxwithenablepin_1_q1),
    ._0x2(_16_bitmuxwithenablepin_1_q2), ._0x3(_16_bitmuxwithenablepin_1_q3),
    ._0x4(_16_bitmuxwithenablepin_1_q4), ._0x5(_16_bitmuxwithenablepin_1_q5),
    ._0x6(_16_bitmuxwithenablepin_1_q6), ._0x7(_16_bitmuxwithenablepin_1_q7),
    ._0x8(_16_bitmuxwithenablepin_1_q8), ._0x9(_16_bitmuxwithenablepin_1_q9),
    ._0xA(_16_bitmuxwithenablepin_1_q10), ._0xB(_16_bitmuxwithenablepin_1_q11),
    ._0xC(_16_bitmuxwithenablepin_1_q12), ._0xD(_16_bitmuxwithenablepin_1_q13),
    ._0xE(_16_bitmuxwithenablepin_1_q14), ._0xF(_16_bitmuxwithenablepin_1_q15), .Q_0(alu_regctrl_1_q_0),
    .Q_1(alu_regctrl_1_q_1), .Q_2(alu_regctrl_1_q_2), .Q_3(alu_regctrl_1_q_3), .Q_4(alu_regctrl_1_q_4),
    .Q_5(alu_regctrl_1_q_5), .Q_6(alu_regctrl_1_q_6), .Q_7(alu_regctrl_1_q_7), .Q_8(alu_regctrl_1_q_8),
    .Q_9(alu_regctrl_1_q_9), .Q_A(alu_regctrl_1_q_a), .RST(alu_regctrl_1_rst));  // open: Q_B, Q_C, Q_D, Q_E, Q_F
  ALU_RegRST alu_regrst_1 (.D(A), .RST(alu_regctrl_1_rst), .Q(alu_regrst_1_q));
  ALU_RegRST alu_regrst_2 (.D(B), .RST(alu_regctrl_1_rst), .Q({alu_regrst_2_q_2, alu_regrst_2_q}));
  not not_1 (not_1_out, CLK);
  not not_2 (not_2_out, CLK);
  // _16_BitRegister _16_bitregister_1: pin names not known; wires that end beside it: alu_regrst_1_q, alu_regctrl_1_q_0
  // Not not_3 has open pins: in=not_1_out, out=open
  // _16_BitRegister _16_bitregister_2: pin names not known; wires that end beside it: {alu_regrst_2_q_2, alu_regrst_2_q}, alu_regctrl_1_q_0
  // Not not_4 has open pins: in=not_2_out, out=open
  Add #(.Bits(16)) add_1 (.a(undriven), .b(undriven_2), .c_i(Carry_In), .s(Sum), .c_o(Carry_Out));
  not not_5 (not_5_out, CLK);
  not not_6 (not_6_out, CLK);
  // _16_BitRegister _16_bitregister_3: pin names not known; wires that end beside it: alu_regrst_1_q, alu_regctrl_1_q_1
  // Not not_7 has open pins: in=not_5_out, out=open
  // _16_BitRegister _16_bitregister_4: pin names not known; wires that end beside it: {alu_regrst_2_q_2, alu_regrst_2_q}, alu_regctrl_1_q_1
  // Not not_8 has open pins: in=not_6_out, out=open
  Sub #(.Bits(16)) sub_1 (.a(undriven_3), .b(undriven_4), .c_i(Borrow_In), .s(Sub), .c_o(Borrow_Out));
  not not_9 (not_9_out, CLK);
  // Not not_10 has open pins: in=not_9_out, out=open
  not not_11 (not_11_out, CLK);
  // Not not_12 has open pins: in=not_11_out, out=open
  // _16_BitRegister _16_bitregister_5: pin names not known; wires that end beside it: alu_regrst_1_q, alu_regctrl_1_q_2
  // _16_BitRegister _16_bitregister_6: pin names not known; wires that end beside it: {alu_regrst_2_q_2, alu_regrst_2_q}, alu_regctrl_1_q_2
  Mul #(.Signed("true"), .Bits(16)) mul_1 (.a(undriven_5), .b(undriven_6), .mul({mul_1_mul, mul_low}));
  not not_13 (not_13_out, CLK);
  // Not not_14 has open pins: in=not_13_out, out=open
  not not_15 (not_15_out, CLK);
  // Not not_16 has open pins: in=not_15_out, out=open
  // _16_BitRegister _16_bitregister_7: pin names not known; wires that end beside it: alu_regrst_1_q, alu_regctrl_1_q_3
  // _16_BitRegister _16_bitregister_8: pin names not known; wires that end beside it: {alu_regrst_2_q_2, alu_regrst_2_q}, alu_regctrl_1_q_3
  Mul #(.Signed("true"), .Bits(16)) mul_2 (.a(undriven_7), .b(undriven_8), .mul({mul_high, mul_2_mul}));
  not not_17 (not_17_out, CLK);
  // Not not_18 has open pins: in=not_17_out, out=open
  not not_19 (not_19_out, CLK);
  // Not not_20 has open pins: in=not_19_out, out=open
  // _16_BitRegister _16_bitregister_9: pin names not known; wires that end beside it: alu_regrst_1_q, alu_regctrl_1_q_4
  // _16_BitRegister _16_bitregister_10: pin names not known; wires that end beside it: {alu_regrst_2_q_2, alu_regrst_2_q}, alu_regctrl_1_q_4
  _16_BitAndOP _16_bitandop_1 (.A(undriven_9), .B(undriven_10), .Q(AND));
  not not_21 (not_21_out, CLK);
  // Not not_22 has open pins: in=not_21_out, out=open
  not not_23 (not_23_out, CLK);
  // Not not_24 has open pins: in=not_23_out, out=open
  // _16_BitRegister _16_bitregister_11: pin names not known; wires that end beside it: alu_regrst_1_q, alu_regctrl_1_q_5
  // _16_BitRegister _16_bitregister_12: pin names not known; wires that end beside it: {alu_regrst_2_q_2, alu_regrst_2_q}, alu_regctrl_1_q_5
  _16_BitXorOP _16_bitxorop_1 (.A(undriven_11), .B(undriven_12), .Q(XOR));
  not not_25 (not_25_out, CLK);
  // Not not_26 has open pins: in=not_25_out, out=open
  not not_27 (not_27_out, CLK);
  // Not not_28 has open pins: in=not_27_out, out=open
  // _16_BitRegister _16_bitregister_13: pin names not known; wires that end beside it: alu_regrst_1_q, alu_regctrl_1_q_6
  // _16_BitRegister _16_bitregister_14: pin names not known; wires that end beside it: {alu_regrst_2_q_2, alu_regrst_2_q}, alu_regctrl_1_q_6
  _16_BitOrOP _16_bitorop_1 (.A(undriven_13), .B(undriven_14), .Q(OR));
  not not_29 (not_29_out, CLK);
  // _16_BitRegister _16_bitregister_15: pin names not known; wires that end beside it: alu_regrst_1_q, alu_regctrl_1_q_7
  // Not not_30 has open pins: in=not_29_out, out=open
  _16_BitNotOP _16_bitnotop_1 (.D(undriven_15), .Q(Not));
  not not_31 (not_31_out, CLK);
  // Not not_32 has open pins: in=not_31_out, out=open
  not not_33 (not_33_out, CLK);
  not not_34 (not_34_out, not_33_out);
  // _16_BitRegister _16_bitregister_16: pin names not known; wires that end beside it: alu_regrst_1_q, alu_regctrl_1_q_8
  Register #(.Bits(5)) _5_bit_reg (.D(alu_regrst_2_q), .C(not_34_out), .en(alu_regctrl_1_q_8), .Q(_5_bit_reg_q));
  BarrelShifter #(.Bits(16), .barrelShifterMode("arithmetic"), .direction("right")) barrelshifter_1 (
    .in(undriven_16), .shift(_5_bit_reg_q), .out(SAR));
  not not_35 (not_35_out, CLK);
  // Not not_36 has open pins: in=not_35_out, out=open
  not not_37 (not_37_out, CLK);
  not not_38 (not_38_out, not_37_out);
  // _16_BitRegister _16_bitregister_17: pin names not known; wires that end beside it: alu_regrst_1_q, alu_regctrl_1_q_9
  Register #(.Bits(5)) _5_bit_reg_2 (.D(alu_regrst_2_q), .C(not_38_out), .en(alu_regctrl_1_q_9), .Q(_5_bit_reg_2_q));
  BarrelShifter #(.Bits(16), .direction("right")) barrelshifter_2 (.in(undriven_17), .shift(_5_bit_reg_2_q), .out(SHR));
  not not_39 (not_39_out, CLK);
  // Not not_40 has open pins: in=not_39_out, out=open
  not not_41 (not_41_out, CLK);
  not not_42 (not_42_out, not_41_out);
  // _16_BitRegister _16_bitregister_18: pin names not known; wires that end beside it: alu_regrst_1_q, alu_regctrl_1_q_a
  Register #(.Bits(5)) _5_bit_reg_3 (.D(alu_regrst_2_q), .C(not_42_out), .en(alu_regctrl_1_q_a), .Q(_5_bit_reg_3_q));
  BarrelShifter #(.Bits(16)) barrelshifter_3 (.in(undriven_18), .shift(_5_bit_reg_3_q), .out(SHL));
endmodule
