// Digital circuit RegisterFile.dig as structural Verilog
module RegisterFile (
  input  CLK,
  input  [15:0] D,
  input  WE,
  input  [7:0] ADDR,
  input  SEL_BRAM,
  output [15:0] Data_Read
);

  wire and_1_out, and_2_out, not_1_out, not_2_out, not_3_out;
  wire [15:0] alu_regrst_1_q, alu_regrst_2_q, alu_regrst_3_q, blockramdualport_1_d, decoder_1_out_0,
       multiplexer_1_out, register_3_q, register_5_q, register_6_q, register_7_q, register_8_q, register_9_q,
       register_10_q, register_11_q, register_12_q, register_13_q, register_14_q, register_15_q,
       register_16_q;
  wire [63:0] register_1_q;

  Decoder #(.Selector_Bits(4)) decoder_1 (
    .sel(ADDR[3:0]), .out_0(decoder_1_out_0[0]), .out_1(decoder_1_out_0[1]), .out_2(decoder_1_out_0[2]),
    .out_3(decoder_1_out_0[3]), .out_4(decoder_1_out_0[4]), .out_5(decoder_1_out_0[5]),
    .out_6(decoder_1_out_0[6]), .out_7(decoder_1_out_0[7]), .out_8(decoder_1_out_0[8]),
    .out_9(decoder_1_out_0[9]), .out_10(decoder_1_out_0[10]), .out_11(decoder_1_out_0[11]),
    .out_12(decoder_1_out_0[12]), .out_13(decoder_1_out_0[13]), .out_14(decoder_1_out_0[14]),
    .out_15(decoder_1_out_0[15]));
  ALU_RegRST alu_regrst_1 (.D(decoder_1_out_0), .RST(not_1_out), .Q(alu_regrst_1_q));
  not not_1 (not_1_out, and_1_out);
  not not_2 (not_2_out, SEL_BRAM);
  and and_1 (and_1_out, not_2_out, WE);
  and and_2 (and_2_out, WE, SEL_BRAM);
  Register #(.Bits(16)) register_1 (.D(D), .C(CLK), .en(alu_regrst_1_q[0]), .Q(register_1_q[15:0]));
  Register #(.Bits(16)) register_2 (.D(D), .C(CLK), .en(alu_regrst_1_q[1]), .Q(register_1_q[31:16]));
  Register #(.Bits(16)) register_3 (.D(D), .C(CLK), .en(alu_regrst_1_q[2]), .Q(register_3_q));
  Register #(.Bits(16)) register_4 (.D(D), .C(CLK), .en(alu_regrst_1_q[3]), .Q(register_1_q[63:48]));
  BlockRAMDualPort #(.AddrBits(8), .Bits(16)) blockramdualport_1 (
    .A(ADDR), .Din(D), .str(and_2_out), .C(CLK), .D(blockramdualport_1_d));
  Register #(.Bits(16)) register_5 (.D(D), .C(CLK), .en(alu_regrst_1_q[4]), .Q(register_5_q));
  Register #(.Bits(16)) register_6 (.D(D), .C(CLK), .en(alu_regrst_1_q[5]), .Q(register_6_q));
  Register #(.Bits(16)) register_7 (.D(D), .C(CLK), .en(alu_regrst_1_q[6]), .Q(register_7_q));
  Register #(.Bits(16)) register_8 (.D(D), .C(CLK), .en(alu_regrst_1_q[7]), .Q(register_8_q));
  Register #(.Bits(16)) register_9 (.D(D), .C(CLK), .en(alu_regrst_1_q[8]), .Q(register_9_q));
  Register #(.Bits(16)) register_10 (.D(D), .C(CLK), .en(alu_regrst_1_q[9]), .Q(register_10_q));
  Register #(.Bits(16)) register_11 (.D(D), .C(CLK), .en(alu_regrst_1_q[10]), .Q(register_11_q));
  Register #(.Bits(16)) register_12 (.D(D), .C(CLK), .en(alu_regrst_1_q[11]), .Q(register_12_q));
  Register #(.Bits(16)) register_13 (.D(D), .C(CLK), .en(alu_regrst_1_q[12]), .Q(register_13_q));
  Register #(.Bits(16)) register_14 (.D(D), .C(CLK), .en(alu_regrst_1_q[13]), .Q(register_14_q));
  Register #(.Bits(16)) register_15 (.D(D), .C(CLK), .en(alu_regrst_1_q[14]), .Q(register_15_q));
  Register #(.Bits(16)) register_16 (.D(D), .C(CLK), .en(alu_regrst_1_q[15]), .Q(register_16_q));
  // _256bits_regRst _256bits_regrst_1: pin names not known; wires that end beside it: {register_1_q[63:48], register_3_q, register_1_q[31:0]}, {register_8_q, register_7_q, register_6_q, register_5_q}, {register_12_q, register_11_q, register_10_q, register_9_q}, {register_16_q, register_15_q, register_14_q, register_13_q}, and_1_out
  Multiplexer #(.Selector_Bits(4), .Bits(16)) multiplexer_1 (
    .sel(ADDR[3:0]), .out(multiplexer_1_out));  // open: in_0, in_1, in_2, in_3, in_4, in_5, in_6, in_7, in_8, in_9, in_10, in_11, in_12, in_13, in_14, in_15
  not not_3 (not_3_out, SEL_BRAM);
  ALU_RegRST alu_regrst_2 (.D(multiplexer_1_out), .RST(SEL_BRAM), .Q(alu_regrst_2_q));
  ALU_RegRST alu_regrst_3 (.D(blockramdualport_1_d), .RST(not_3_out), .Q(alu_regrst_3_q));
  assign Data_Read = alu_regrst_2_q | alu_regrst_3_q;  // Or or_1, 16 bits wide
endmodule
